# Fritzing sketch Car_Remote_Sketch (saved by Fritzing 0.9.10b)
breadboards: 1

parts:
  Part1 = Arduino Mega ADK (Rev3)
  DI1 = 7-Segment LED Display [package=THT]
  Part2 = Color Sensor Breakout ADJD-S311  # not connected
  Part3 = Bluetooth HC-05 Macho  # not connected
  DFRobot_DFPlayer_Mini1 = DFRobot DFPlayer Mini [part_number=DFR0299]
  Part4 = Thumb Joystick
  R1 = Resistor [tolerance=±5% power=0.25 resistance=1k package=THT]
  R2 = Resistor [tolerance=±5% power=0.25 resistance=1k package=THT]
  R3 = Resistor [tolerance=±5% power=0.25 resistance=1k package=THT]
  R4 = Resistor [tolerance=±5% power=0.25 resistance=1k package=THT]
  J1 = Piezo Speaker
  LED1 = LEDs [package=led10mm]
  R5 = Resistor [tolerance=±5% power=0.25 resistance=1k package=THT]

nets:
  N1: Part1.A14, Part4.HORZ
  N2: Part1.A15, Part4.VERT
  VCC: Part1.5V, DFRobot_DFPlayer_Mini1.VCC, Part4.VCC, R1.Pin_0
  N3: Part1.D28, DI1.cathodeG
  N4: Part1.D29, DI1.cathodeF
  N5: Part1.D30, DI1.cathodeA
  N6: Part1.D31, DI1.cathodeB
  N7: Part1.D32, DI1.cathodeC
  N8: Part1.D33, DI1.cathodeDP
  N9: Part1.D34, DI1.cathodeE
  N10: Part1.D35, DI1.cathodeD
  N11: Part1.D41, Part4.SEL
  N12: Part1.D45, LED1.A
  N13: Part1.D51/MOSI, R2.Pin_1
  N14: Part1.D52/SCK, DFRobot_DFPlayer_Mini1.TX
  N15: Part1.D53/SS, DFRobot_DFPlayer_Mini1.RX
  GND: Part1.GND, DFRobot_DFPlayer_Mini1.GND-1, DFRobot_DFPlayer_Mini1.GND-2, Part4.GND, R4.Pin_0, R5.Pin_0
  N16: DI1.commAnode#7, R1.Pin_1
  N17: DFRobot_DFPlayer_Mini1.SPK_1, J1.pin1
  N18: DFRobot_DFPlayer_Mini1.SPK_2, J1.pin2
  N19: R2.Pin_0, R3.Pin_1
  N20: R3.Pin_0, R4.Pin_1
  N21: LED1.C, R5.Pin_1
