# Fritzing sketch Car_Sketch (saved by Fritzing 0.9.10b)
breadboards: 1

parts:
  J1 = Piezo Speaker
  Part1 = Bluetooth HC-05 Macho  # not connected
  Part2 = Arduino Uno (Rev3) - ICSP
  R1 = Resistor [tolerance=±5% power=0.25 resistance=1k package=THT]
  R2 = Resistor [tolerance=±5% power=0.25 resistance=1k package=THT]
  R3 = Resistor [tolerance=±5% power=0.25 resistance=1k package=THT]
  IC1 = H-Bridge [package=THT]
  HC-SR04_Sensor_1 = HC-SR04 Ultrasonic Distance Sensor
  HC-SR04_Sensor_2 = HC-SR04 Ultrasonic Distance Sensor
  HC-SR04_Sensor_3 = HC-SR04 Ultrasonic Distance Sensor
  HC-SR04_Sensor_4 = HC-SR04 Ultrasonic Distance Sensor
  BAT1 = Battery Holders [package=battery-aa]
  BAT2 = Battery Holders [package=battery-aa]
  BAT3 = Battery Holders [package=battery-aa]
  BAT4 = Battery Holders [package=battery-aa]

nets:
  GND: J1.pin1, Part2.GND, R3.Pin_0, HC-SR04_Sensor_1.GND, HC-SR04_Sensor_2.GND, HC-SR04_Sensor_3.GND, HC-SR04_Sensor_4.GND
  N1: J1.pin2, Part2.A0
  N2: Part2.A2, HC-SR04_Sensor_1.ECHO
  N3: Part2.A3, HC-SR04_Sensor_4.ECHO
  N4: Part2.A4/SDA, HC-SR04_Sensor_3.ECHO
  N5: Part2.A5/SCL, HC-SR04_Sensor_2.ECHO
  N6: Part2.ICSP_MISO, Part2.D12/MISO, HC-SR04_Sensor_4.TRIG
  N7: Part2.D8, IC1.3Y
  N8: Part2.D9_PWM, IC1.4Y
  N9: Part2.D11_PWM/MOSI, R1.Pin_1
  N10: Part2.D13/SCK, HC-SR04_Sensor_1.TRIG
  N11: Part2.D2, HC-SR04_Sensor_2.TRIG
  N12: Part2.D3_PWM, IC1.3_4EN
  N13: Part2.D4, HC-SR04_Sensor_3.TRIG
  N14: Part2.D5_PWM, IC1.1_2EN
  N15: Part2.D6_PWM, IC1.1Y
  N16: Part2.D7, IC1.2Y
  VCC: Part2.5V, HC-SR04_Sensor_1.VCC, HC-SR04_Sensor_2.VCC, HC-SR04_Sensor_3.VCC, HC-SR04_Sensor_4.VCC
  N17: R1.Pin_0, R2.Pin_1
  N18: R2.Pin_0, R3.Pin_1
  N19: IC1.GND3, BAT1.+
  N20: IC1.VCC1, BAT4.-
  N21: BAT1.-, BAT2.+
  N22: BAT2.-, BAT3.+
  N23: BAT3.-, BAT4.+
